// Logisim project Car_design.circ as structural Verilog: 1 circuit, main circuit main
module main (
  input  KB,
  input  KR,
  input  in_3,
  input  KS,
  input  F,
  output L3,
  output L2,
  output L1,
  output R3,
  output R2,
  output R1
);

  wire and_1_out, and_2_out, and_3_out, and_5_out, and_6_out, and_7_out, and_8_out, and_9_out, and_10_out,
       clock_1_out, clock_2_out, clock_3_out, j_k_ff_1_q, j_k_ff_1_qn, j_k_ff_2_q, j_k_ff_2_qn, j_k_ff_3_q,
       j_k_ff_3_qn, n74138_1_pin4, n74138_1_pin7, n74138_1_pin11, n74138_1_pin13, n74138_1_pin14, not_1_out,
       not_2_out, not_3_out, not_4_out, or_1_out, or_2_out, or_3_out, or_4_out, or_5_out, or_6_out, or_7_out,
       or_8_out, or_9_out, or_10_out;

  J_K_Flip_Flop j_k_ff_1 (
    .J(1'b1), .K(1'b1), .clk(clock_1_out), .Q(j_k_ff_1_q), .Qn(j_k_ff_1_qn));  // open: preset, reset
  Clock clock_1 (.out(clock_1_out));
  J_K_Flip_Flop j_k_ff_2 (
    .J(and_3_out), .K(KR), .clk(clock_2_out), .Q(j_k_ff_2_q), .Qn(j_k_ff_2_qn));  // open: preset, reset
  Clock clock_2 (.out(clock_2_out));
  J_K_Flip_Flop j_k_ff_3 (
    .J(and_2_out), .K(j_k_ff_2_q), .clk(clock_3_out), .Q(j_k_ff_3_q), .Qn(j_k_ff_3_qn));  // open: preset, reset
  Clock clock_3 (.out(clock_3_out));
  _74138 #(.ShowInternalStructure("true")) u_74138_1 (
    .pin1(KB), .pin2(KR), .pin3(in_3), .pin4(n74138_1_pin4), .pin5(n74138_1_pin4), .pin6(KS),
    .pin7(n74138_1_pin7), .pin14(n74138_1_pin14), .pin13(n74138_1_pin13), .pin11(n74138_1_pin11));  // open: pin15, pin12, pin10, pin9
  not not_1 (not_1_out, n74138_1_pin14);
  not not_2 (not_2_out, n74138_1_pin13);
  not not_3 (not_3_out, n74138_1_pin11);
  not not_4 (not_4_out, n74138_1_pin7);
  and and_1 (and_1_out, KS, F);
  and and_2 (and_2_out, j_k_ff_1_qn, j_k_ff_2_qn);
  and and_3 (and_3_out, j_k_ff_1_qn, j_k_ff_3_qn);
  and and_4 (KR, j_k_ff_1_q, j_k_ff_3_q);
  or or_1 (or_1_out, not_1_out, not_2_out);
  or or_2 (or_2_out, not_1_out, not_3_out);
  or or_3 (or_3_out, or_1_out, not_4_out);
  or or_4 (or_4_out, or_2_out, not_4_out);
  and and_5 (and_5_out, in_3, j_k_ff_1_q);
  and and_6 (and_6_out, in_3, j_k_ff_2_q);
  and and_7 (and_7_out, in_3, j_k_ff_3_q);
  and and_8 (and_8_out, KR, j_k_ff_1_q);
  and and_9 (and_9_out, KR, j_k_ff_2_q);
  and and_10 (and_10_out, KR, j_k_ff_3_q);
  or or_5 (or_5_out, or_3_out, and_5_out);
  or or_6 (or_6_out, or_3_out, and_6_out);
  or or_7 (or_7_out, or_3_out, and_7_out);
  or or_8 (or_8_out, or_4_out, and_8_out);
  or or_9 (or_9_out, or_4_out, and_9_out);
  or or_10 (or_10_out, or_4_out, and_10_out);
  or or_11 (L3, or_5_out, and_1_out);
  or or_12 (L2, or_6_out, and_1_out);
  or or_13 (L1, or_7_out, and_1_out);
  or or_14 (R3, or_8_out, and_1_out);
  or or_15 (R2, or_9_out, and_1_out);
  or or_16 (R1, or_10_out, and_1_out);
  // also tied to GND on the sheet: n74138_1_pin4

  // Notes on the sheet:
  //   KL
  //   Q1
  //   Q3
  //   Q2
endmodule
