// Logisim project test02.circ as structural Verilog: 1 circuit, main circuit main
module main (
  input  in_1,
  input  in_2,
  input  in_3,
  input  in_4,
  output F
);

  wire n74138_1_pin4, n74138_1_pin5, n74138_1_pin6, n74138_1_pin7, n74138_1_pin11, n74138_1_pin12,
       n74138_1_pin15, nand_1_out, nand_2_out, not_1_out;

  not not_1 (not_1_out, in_1);
  _74138 #(.ShowInternalStructure("true")) u_74138_1 (
    .pin1(in_2), .pin2(in_3), .pin3(in_4), .pin4(n74138_1_pin4), .pin5(n74138_1_pin5), .pin6(n74138_1_pin6),
    .pin7(n74138_1_pin7), .pin15(n74138_1_pin15), .pin12(n74138_1_pin12), .pin11(n74138_1_pin11));  // open: pin14, pin13, pin10, pin9
  or or_1 (F, nand_1_out, nand_2_out);
  nand nand_1 (nand_1_out, in_1, n74138_1_pin15, n74138_1_pin12);
  nand nand_2 (nand_2_out, n74138_1_pin11, n74138_1_pin7, not_1_out);
  not not_2 (n74138_1_pin5, 1'b0);
  not not_3 (n74138_1_pin4, 1'b0);
  // also tied to VCC on the sheet: n74138_1_pin6

  // Notes on the sheet:
  //   A
  //   B
  //   C
  //   D
endmodule
